// Logisim project 4_bits_register.circ as structural Verilog: 1 circuit, main circuit main
module main (
  input  data0,
  input  data1,
  input  data2,
  input  data3,
  input  write_enable,
  output output0,
  output output1,
  output output2,
  output output3
);

  wire and_1_out, clock_1_out;

  Clock clock_1 (.out(clock_1_out));
  and and_1 (and_1_out, clock_1_out, write_enable);
  flip_flop flip_flop_1 (.clock(and_1_out), .data(data0), .output_q(output0));
  flip_flop flip_flop_2 (.clock(and_1_out), .data(data1), .output_q(output1));
  flip_flop flip_flop_3 (.clock(and_1_out), .data(data2), .output_q(output2));
  flip_flop flip_flop_4 (.clock(and_1_out), .data(data3), .output_q(output3));
endmodule
