// Logisim project xor.circ as structural Verilog: 1 circuit, main circuit xor_gate
module xor_gate (
  input  input1,
  input  input2,
  output output1
);

  wire and_1_out, not_1_out, or_1_out;

  and and_1 (and_1_out, input1, input2);
  or or_1 (or_1_out, input1, input2);
  not not_1 (not_1_out, and_1_out);
  and and_2 (output1, not_1_out, or_1_out);
endmodule
